# Fritzing sketch Edukit3-pico (saved by Fritzing 0.9.3b)
breadboards: 2

parts:
  Mod1 = Raspberry Pi Pico
  IC1 = H-Bridge [package=THT]
  hc-sr1 = hc-sr04
  VCC1 = 4 x AAA Battery Mount  # not connected
  IR1 = TSOP312.., 314.. [package=THT]
  Part1 = KY-033 Tracing Black White Line Hunting Sensor Module For Arduino
  M1 = DC Motor
  M2 = DC Motor

nets (from the schematic view):
  Echo: Mod1.pin_1, hc-sr1.Echo
  Trig: Mod1.pin_2, hc-sr1.Trig
  N1: Mod1.pin_3, Mod1.pin_8, Mod1.pin_13, Mod1.pin_18, Mod1.pin_23, Mod1.pin_28, Mod1.pin_33, Mod1.pin_38
  M1a: Mod1.pin_19, IC1.1A
  M1b: Mod1.pin_20, IC1.2A
  M2b: Mod1.pin_21, IC1.3A
  M2a: Mod1.pin_22, IC1.4A
  N2: Mod1.pin_26, IR1.Data
  Line: Mod1.pin_27, Part1.S
  3.3V: Mod1.pin_36, IC1.1_2EN, IC1.VCC1, hc-sr1.VCC, IR1.Vs, Part1.V+
  5V: Mod1.pin_39, IC1.VCC2
  N3: IC1.1Y, M1.pin_1
  GND: IC1.GND1, IC1.GND3, hc-sr1.GND, IR1.GND, Part1.GND
  N4: IC1.2Y, M1.pin_2
  N5: IC1.3Y, M2.pin_2
  N6: IC1.4Y, M2.pin_1

custom parts:
  Raspberry Pi Pico: Raspberry Pi Pico. Based around the RP2040 microcontroller the Pico is a low cost microcontroller device bringing Raspberry Pi quality, cost, and easy of use to the microcontroller space. Jan 2021, Split part in to two versions: tht (this one) and SMD. This one will drill holes for a .1 in header in pcb to allow plugging in the module as well as providing pads to solder the module to the top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
  KY-033 Tracing Black White Line Hunting Sensor Module For Arduino: Tracing Black White Line Hunting Sensor Module For Arduino Description: This is KY-033 tracking sensor. The KY-033 measures the intensity of infrared radiation and delivers it as an analog output voltage. Features: Operating voltage: 2.5 - 12V(cannot over12V) working current: 18mA-20mA at 5V Enhanced accuracy Documents: http://www.vishay.com/docs/83760/tcrt5000.pdf
